# Fritzing sketch Arduino-Stepper (saved by Fritzing 0.9.3b)
breadboards: 1

parts:
  Part1 = Arduino Uno (Rev3)
  M2 = Stepper Motor - Unipolar
  U1 = Mystery Part - 11 pins [chip_label=ULN2003 package=THT]

nets:
  N1: Part1.D8, U1.In1
  N2: Part1.D9_PWM, U1.In2
  N3: Part1.D10_PWM/SS, U1.In3
  N4: Part1.D11_PWM/MOSI, U1.In4
  GND: Part1.GND, U1.Gnd
  5V: Part1.5V, U1.Vcc
  N5: M2.A, U1.P
  N6: M2.COMMON_1, M2.COMMON_2, U1.R
  N7: M2.C, U1.O
  N8: M2.B, U1.Y
  N9: M2.D, U1.B

custom parts:
  Mystery Part - 11 pins: A dummy, proxy, ersatz, stand-in part for whatever you want. With 11 pins on a 100 mil inline pin header footprint.
