# Fritzing sketch Arduino-Ultrasonic-Buzzer (saved by Fritzing 0.9.3b)
breadboards: 1

parts:
  Part1 = Arduino Uno (Rev3)
  J1 = Piezo Speaker
  HC-SR04_Sensor_1 = HC-SR04 Ultrasonic Distance Sensor
  R1 = Resistor [tolerance=±5% resistance=100 package=THT]

nets:
  N1: Part1.D9_PWM, R1.Pin_0
  GND: Part1.GND, J1.pin2, HC-SR04_Sensor_1.ECHO
  N2: Part1.D4, HC-SR04_Sensor_1.GND
  N3: Part1.D5_PWM, HC-SR04_Sensor_1.TRIG
  5V: Part1.5V, HC-SR04_Sensor_1.VCC
  N4: J1.pin1, R1.Pin_1
